# Fritzing sketch elec (saved by Fritzing 0.9.3b)

parts:
  R2 = Resistor [tolerance=±5% resistance=10k package="0402 [SMD]"]
  R1 = PHOTOCELL [package=photocell]
  RHT1 = Humidity and Temperature Sensor RHT03
  J1 = Basic Servo
  Part1 = Arduino Uno (Rev3) - ICSP
  Part2 = Soil Moisture Sensor
  Part3 = Soil Moisture Sensor
  LED2 = smd LED [color="Yellow (595nm)" package="0603 [SMD]"]
  LED1 = smd LED [color="Red (633nm)" package="0603 [SMD]"]
  R3 = Resistor [tolerance=±5% resistance=10k package="0402 [SMD]"]
  R4 = Resistor [tolerance=±5% resistance=10k package="0402 [SMD]"]

nets:
  N1: R2.Pin_1, R1.P$2
  N2: RHT1.Vcc, Part1.D2
  N3: RHT1.GND_1, RHT1.GND_2
  N4: J1.pulse, Part1.A5/SCL
  N5: Part1.A3, Part3.SIG
  N6: Part1.A4/SDA, Part2.SIG
  N7: Part1.D4, LED2.anode
  N8: LED2.cathode, R4.Pin_1
  N9: LED1.cathode, R3.Pin_1
